# Fritzing sketch nucleo (saved by Fritzing 0.9.5d)
breadboards: 1

parts:
  J1 = STM32 Nucleo boards
  R1 = Resistor [tolerance=±5% resistance=220 package="1206 [SMD]"]
  R2 = Resistor [tolerance=±5% resistance=220 package="1206 [SMD]"]
  R3 = Resistor [tolerance=±5% resistance=220 package="1206 [SMD]"]
  part = female pin header, 1 pin [form="♀ (female)"]  # not connected
  J2 = female pin header, 1 pin [form="♀ (female)"]  # not connected
  J3 = female pin header, 1 pin [form="♀ (female)"]  # not connected
  J4 = female pin header, 1 pin [form="♀ (female)"]  # not connected
  J5 = female pin header, 1 pin [form="♀ (female)"]  # not connected
  LED1 = RGB LED - (4 legs) [package="5 mm [THT]"]
  R4 = PHOTOCELL [package=photocell]
  R5 = Resistor [tolerance=±5% resistance=220 package="1206 [SMD]"]
  J6 = Piezo Speaker
  DHT1 = DHT11 Humitidy and Temperature Sensor (3 pins)
  KY-1 = Keyes Relay [package=THT]
  LED2 = LEDs [package=led10mm]
  Power_plug1 = Power plug

nets:
  N1: J1.A0, R4.P$2, R5.Pin_1
  N2: J1.D8, R3.Pin_0
  N3: J1.D9_PWM, R2.Pin_0
  N4: J1.D10_PWM/SS, R1.Pin_0
  N5: J1.GND#1157, R5.Pin_0, J6.pin1, DHT1.GND, KY-1.ground
  N6: J1.D2, KY-1.signal
  N7: J1.D4, J6.pin2
  N8: J1.D7, DHT1.DATA
  5V: J1.5V, R4.P$1, DHT1.VDD, KY-1.power
  N9: R1.Pin_1, LED1.red_cathode
  N10: R2.Pin_1, LED1.green_cathode
  N11: R3.Pin_1, LED1.blue_cathode
  N12: KY-1.C, Power_plug1.VCC
  N13: KY-1.NO, LED2.A
  N14: LED2.C, Power_plug1.GND

custom parts:
  DHT11 Humitidy and Temperature Sensor (3 pins): DHT11 Humidity and Temperature Sensor (3 pins) from the design created by John De Cristofaro for Adafruit Industries.
  Keyes Relay: The Keyes 5V relay module is suitable for SCM development, home appliance control. It uses a 5V~12V TIL control signal which can control DC / AC signal.
  LEDs: LEDs Standard schematic elements and footprints for 5mm, 3mm, 1206, and 0603 sized LEDs. 5mm - Spark Fun Electronics SKU : COM-00529 (and others)
